# Fritzing sketch agrosensor (saved by Fritzing 0.9.3b)
circuit board: 13.1557cm x 5.6027cm
breadboards: 1

parts:
  DS1 = DS18B20 1-Wire Temperature Sensor [part_number=DS18B20]
  WeMos_D1_Mini1 = WeMos D1 Mini
  Part1 = Soil Moisture Sensor
  TP4056 = TP4056 Module [part_number=HW-107]
  Battery_14500 = Battery Holders [package=battery-aa]
  D1 = SOLAR-IXYS [package=solarbit-12x1]
  R1 = Resistor [tolerance=±5% resistance=220 package=THT]

nets:
  GND: DS1.GND, WeMos_D1_Mini1.G, Part1.GND, TP4056.OUT-#1, R1.Pin_1
  N1: DS1.DQ, WeMos_D1_Mini1.D3, R1.Pin_0
  VDD: DS1.VDD, WeMos_D1_Mini1.3V3
  N2: WeMos_D1_Mini1.D1, Part1.VCC, TP4056.OUT-#4
  N3: TP4056.GND, D1.C
  N4: TP4056.BAT-, Battery_14500.-
  N5: TP4056.BAT+, Battery_14500.+
  N6: TP4056.VCC, D1.A

custom parts:
  TP4056 Module: TP4056 Lithium Battery Charge Management Module Links: TP4056 website
